# Fritzing sketch Schematic_MecanumCar (saved by Fritzing 1.0.2b)

parts:
  Mod1 = Amica NodeMCU DEVKIT 1.0
  U1 = LIPO-2000mAh [package=lipo-2000]
  U2 = LIPO-2000mAh [package=lipo-2000]
  TP1 = TP4056 [chip_label=TP4056 package="DIP (Dual Inline) [THT]"]
  Part1 = Motor Driver 1A Dual TB6612FNG
  Part2 = Motor Driver 1A Dual TB6612FNG
  M4 = DC Motor [voltage_(max)=6V voltage_(min)=3V]
  M5 = DC Motor [voltage_(max)=6V voltage_(min)=3V]
  M6 = DC Motor [voltage_(max)=6V voltage_(min)=3V]
  M7 = DC Motor [voltage_(max)=6V voltage_(min)=3V]
  LED1 = LED - 5mm [color="Red (633nm)" current=0.030A package="5 mm [THT]"]
  LED2 = LED - 5mm [color="Yellow (595nm)" current=0.030A package="5 mm [THT]"]  # not connected
  LED3 = LED - 5mm [color="Green (555nm)" current=0.030A package="5 mm [THT]"]
  R1 = Resistor [tolerance=±5% power=0.25W resistance=1k package=THT]
  R2 = Resistor [tolerance=±5% power=0.25W resistance=1k package=THT]
  R3 = Resistor [tolerance=±5% power=0.25W resistance=1k package=THT]
  R4 = Resistor [tolerance=±5% power=0.25W resistance=47k package=THT]
  R5 = Resistor [tolerance=±5% power=0.25W resistance=33k package=THT]

nets:
  N1: Mod1.pin1, Mod1.pin_10, Part1.B02
  N2: Mod1.pin2, Mod1.pin_9, Mod1.pin_25, Part1.B01
  N3: Mod1.pin8, Part1.GND, M7.pin_2
  N4: Mod1.pin_11, Part1.A02
  N5: Mod1.pin_12, Part2.GND, M5.pin_2
  N6: Mod1.pin_13, Part2.B01
  N7: Mod1.pin_14, Part2.B02
  N8: Mod1.pin_15, Part2.A02
  N9: Mod1.pin_20, R1.Pin_1
  N10: Mod1.pin_21, R3.Pin_1
  N11: Mod1.pin_22, R2.Pin_1
  N12: U1.+, TP1.pin4
  N13: U1.-, U2.+
  N14: U2.-, TP1.pin5
  N15: Part1.VCC, LED1.cathode, LED3.cathode
  N16: Part1.BIN1, M6.pin_1
  N17: Part1.BIN2, M6.pin_2
  N18: Part1.PWMB, M7.pin_1
  N19: Part2.BIN1, M4.pin_1
  N20: Part2.BIN2, M4.pin_2
  N21: Part2.PWMB, M5.pin_1
  N22: R4.Pin_0, R5.Pin_1

notes:
  BMS
  ESP32
  A
  B
  C
  D
  Motor Drivers
  Status-LEDs
  Voltage-Divider

custom parts:
  TP4056: A DIP stand-in part for whatever IC you want. With 6 pins on a 300mil dual inline package (DIP) footprint.
